// Logisim project Digital_Electronics-ATM_simulation.circ as structural Verilog: 3 circuits, main circuit main
module main (
  input  [1:0] in_1,
  input  in_2,
  input  [1:0] in_3,
  input  in_4,
  input  in_5,
  input  in_6,
  input  in_7,
  input  _0___Credit,
  input  [1:0] in_9,
  input  in_10,
  input  [1:0] in_11,
  input  in_12,
  input  [1:0] in_13,
  input  in_14
);

  wire _0, _1, _2, _3, _4, _5, _6, _7, _8, _9, and_1_out, Clear, clock_1_out, clock_2_out, clock_3_out,
       clock_4_out, clock_5_out, clock_6_out, comparator_1_eq, comparator_2_eq, comparator_3_eq,
       comparator_4_eq, demultiplexer_1_out0, demultiplexer_1_out1, demultiplexer_1_out2,
       demultiplexer_1_out3, not_1_out, SET_PIN;
  wire [1:0] counter_1_q;
  wire [3:0] _4___bit_BUS, bcd_adder_2_out_3, bcd_adder_3_out_3, bcd_adder_3_out_4, bcd_adder_4_out_3,
       bcd_adder_5_out_3, bcd_adder_5_out_4, bcd_adder_6_out_3, bcd_adder_7_out_3, bcd_adder_7_out_4,
       bcd_adder_8_out_3, bcd_adder_9_out_3, bcd_adder_9_out_4, bcd_adder_10_out_3, bcd_adder_11_out_3,
       bcd_adder_11_out_4, bcd_adder_12_out_3, bcd_adder_13_out_3, bcd_adder_13_out_4, bcd_adder_14_out_3,
       bcd_adder_15_out_3, BCD_adder_out_3, BCD_adder_out_4, debit_1_out_2, debit_2_out_2, debit_3_out_2,
       debit_4_out_2, debit_5_out_2, debit_6_out_2, debit_7_out_2, debit_circuit_out_2, R1_q, R2_q, R3_q,
       R4_q, ram_1_data, ram_2_data, ram_3_data, ram_4_data;
  wire [31:0] multiplexer_1_out, ram_5_data, ram_6_data, subtractor_1_out;

  Demultiplexer #(.select(2)) demultiplexer_1 (
    .out0(demultiplexer_1_out0), .out1(demultiplexer_1_out1), .out2(demultiplexer_1_out2),
    .out3(demultiplexer_1_out3), .in(in_7), .sel(counter_1_q));  // open: en
  Hex_Digit_Display hex_digit_display_1 (.value(R1_q));  // open: dp
  Counter #(.width(2), .max('h3)) counter_1 (
    .count(SET_PIN), .Q(counter_1_q), .clk(SET_PIN), .clr(Clear));  // open: load, D, carry
  Clock clock_1 (.out(clock_1_out));
  Hex_Digit_Display hex_digit_display_2 (.value(R2_q));  // open: dp
  Hex_Digit_Display hex_digit_display_3 (.value(R3_q));  // open: dp
  or or_1 (_4___bit_BUS[0], _1, _3, _5, _7, _9);
  or or_2 (_4___bit_BUS[1], _2, _3, _6, _7);
  or or_3 (_4___bit_BUS[2], _4, _5, _6, _7);
  or or_4 (_4___bit_BUS[3], _8, _9);
  Hex_Digit_Display hex_digit_display_4 (.value(R4_q));  // open: dp
  Register #(.width(4)) R1 (.D(_4___bit_BUS), .en(demultiplexer_1_out1), .Q(R1_q), .clk(clock_1_out), .clr(Clear));
  Register #(.width(4)) R2 (.D(_4___bit_BUS), .en(demultiplexer_1_out2), .Q(R2_q), .clk(clock_1_out), .clr(Clear));
  Register #(.width(4)) R3 (.D(_4___bit_BUS), .en(demultiplexer_1_out3), .Q(R3_q), .clk(clock_1_out), .clr(Clear));
  Register #(.width(4)) R4 (.D(_4___bit_BUS), .en(demultiplexer_1_out0), .Q(R4_q), .clk(clock_1_out), .clr(Clear));
  Button u__7 (.out(_7));
  Button u__4 (.out(_4));
  Button u__1 (.out(_1));
  Button u__8 (.out(_8));
  Button u__5 (.out(_5));
  Button u__2 (.out(_2));
  Button u__0 (.out(_0));
  Button u_CLEAR (.out(Clear));
  Button u__9 (.out(_9));
  Button u__6 (.out(_6));
  Button u__3 (.out(_3));
  Clock clock_2 (.out(clock_2_out));
  or or_5 (SET_PIN, _8, _5, _7, _9, _4, _3, _1, _2, _0, _6);
  RAM #(.addrWidth(2), .dataWidth(4), .bus("separate")) ram_1 (
    .addr(in_3), .din(R1_q), .data(ram_1_data), .str(in_6), .clk(clock_2_out), .ld(in_5), .clr(in_4));  // open: sel
  RAM #(.addrWidth(2), .dataWidth(4), .bus("separate")) ram_2 (
    .addr(in_9), .din(R2_q), .data(ram_2_data), .str(in_6), .clk(clock_3_out), .ld(in_10), .clr(in_4));  // open: sel
  Clock clock_3 (.out(clock_3_out));
  RAM #(.addrWidth(2), .dataWidth(4), .bus("separate")) ram_3 (
    .addr(in_11), .din(R3_q), .data(ram_3_data), .str(in_6), .clk(clock_4_out), .ld(in_12), .clr(in_4));  // open: sel
  Clock clock_4 (.out(clock_4_out));
  RAM #(.addrWidth(2), .dataWidth(4), .bus("separate")) ram_4 (
    .addr(in_13), .din(R4_q), .data(ram_4_data), .str(in_6), .clk(clock_5_out), .ld(in_14), .clr(in_4));  // open: sel
  Clock clock_5 (.out(clock_5_out));
  Comparator #(.width(4)) comparator_1 (.a(R1_q), .b(ram_1_data), .eq(comparator_1_eq));  // open: gt, lt
  Comparator #(.width(4)) comparator_2 (.a(R2_q), .b(ram_2_data), .eq(comparator_2_eq));  // open: gt, lt
  Comparator #(.width(4)) comparator_3 (.a(R3_q), .b(ram_3_data), .eq(comparator_3_eq));  // open: gt, lt
  Comparator #(.width(4)) comparator_4 (.a(R4_q), .b(ram_4_data), .eq(comparator_4_eq));  // open: gt, lt
  LED Incorrect_Pin (.in(not_1_out));
  not not_1 (not_1_out, and_1_out);
  and and_1 (and_1_out, comparator_1_eq, comparator_2_eq, comparator_3_eq, comparator_4_eq);
  Hex_Digit_Display hex_digit_display_5 (.value(ram_5_data[31:28]));  // open: dp
  Clock clock_6 (.out(clock_6_out));
  LED Correct_Pin (.in(and_1_out));
  Hex_Digit_Display hex_digit_display_6 (.value(ram_5_data[23:20]));  // open: dp
  Hex_Digit_Display hex_digit_display_7 (.value(ram_5_data[27:24]));  // open: dp
  Hex_Digit_Display hex_digit_display_8 (.value(ram_5_data[19:16]));  // open: dp
  Hex_Digit_Display hex_digit_display_9 (.value(ram_5_data[15:12]));  // open: dp
  RAM #(.addrWidth(2), .dataWidth(32), .bus("separate")) ram_5 (
    .addr(in_1), .din(multiplexer_1_out), .data(ram_5_data), .sel(and_1_out), .clk(clock_6_out), .clr(in_2));  // open: str, ld
  RAM #(.addrWidth(2), .dataWidth(32), .bus("separate")) ram_6 (
    .addr(in_1), .data(ram_6_data), .sel(and_1_out), .clk(clock_6_out), .clr(in_2));  // open: din, str, ld
  Hex_Digit_Display hex_digit_display_10 (.value(ram_5_data[7:4]));  // open: dp
  Hex_Digit_Display hex_digit_display_11 (.value(ram_5_data[11:8]));  // open: dp
  Hex_Digit_Display hex_digit_display_12 (.value(ram_5_data[3:0]));  // open: dp
  Subtractor #(.width(32)) subtractor_1 (.a(ram_5_data), .b(ram_6_data), .out(subtractor_1_out));  // open: bin, bout
  BCD_adder BCD_adder (
    .in_1(ram_5_data[3:0]), .in_2(ram_6_data[3:0]), .out_3(BCD_adder_out_3), .out_4(BCD_adder_out_4));
  Debit debit_circuit (.in_1(subtractor_1_out[3:0]), .out_2(debit_circuit_out_2));
  Debit debit_1 (.in_1(subtractor_1_out[7:4]), .out_2(debit_1_out_2));
  Debit debit_2 (.in_1(subtractor_1_out[11:8]), .out_2(debit_2_out_2));
  Debit debit_3 (.in_1(subtractor_1_out[15:12]), .out_2(debit_3_out_2));
  Debit debit_4 (.in_1(subtractor_1_out[19:16]), .out_2(debit_4_out_2));
  Debit debit_5 (.in_1(subtractor_1_out[23:20]), .out_2(debit_5_out_2));
  Debit debit_6 (.in_1(subtractor_1_out[27:24]), .out_2(debit_6_out_2));
  Debit debit_7 (.in_1(subtractor_1_out[31:28]), .out_2(debit_7_out_2));
  BCD_adder bcd_adder_2 (.in_1(BCD_adder_out_4), .in_2(bcd_adder_3_out_3), .out_3(bcd_adder_2_out_3));  // open: out_4
  BCD_adder bcd_adder_3 (
    .in_1(ram_5_data[7:4]), .in_2(ram_6_data[7:4]), .out_3(bcd_adder_3_out_3), .out_4(bcd_adder_3_out_4));
  BCD_adder bcd_adder_4 (.in_1(bcd_adder_3_out_4), .in_2(bcd_adder_5_out_3), .out_3(bcd_adder_4_out_3));  // open: out_4
  BCD_adder bcd_adder_5 (
    .in_1(ram_5_data[11:8]), .in_2(ram_6_data[11:8]), .out_3(bcd_adder_5_out_3), .out_4(bcd_adder_5_out_4));
  BCD_adder bcd_adder_6 (.in_1(bcd_adder_5_out_4), .in_2(bcd_adder_7_out_3), .out_3(bcd_adder_6_out_3));  // open: out_4
  BCD_adder bcd_adder_7 (
    .in_1(ram_5_data[15:12]), .in_2(ram_6_data[15:12]), .out_3(bcd_adder_7_out_3), .out_4(bcd_adder_7_out_4));
  BCD_adder bcd_adder_8 (.in_1(bcd_adder_7_out_4), .in_2(bcd_adder_9_out_3), .out_3(bcd_adder_8_out_3));  // open: out_4
  BCD_adder bcd_adder_9 (
    .in_1(ram_5_data[19:16]), .in_2(ram_6_data[19:16]), .out_3(bcd_adder_9_out_3), .out_4(bcd_adder_9_out_4));
  BCD_adder bcd_adder_10 (
    .in_1(bcd_adder_9_out_4), .in_2(bcd_adder_11_out_3), .out_3(bcd_adder_10_out_3));  // open: out_4
  BCD_adder bcd_adder_11 (
    .in_1(ram_5_data[23:20]), .in_2(ram_6_data[23:20]), .out_3(bcd_adder_11_out_3), .out_4(bcd_adder_11_out_4));
  BCD_adder bcd_adder_12 (
    .in_1(bcd_adder_11_out_4), .in_2(bcd_adder_13_out_3), .out_3(bcd_adder_12_out_3));  // open: out_4
  BCD_adder bcd_adder_13 (
    .in_1(ram_5_data[27:24]), .in_2(ram_6_data[27:24]), .out_3(bcd_adder_13_out_3), .out_4(bcd_adder_13_out_4));
  BCD_adder bcd_adder_14 (
    .in_1(bcd_adder_13_out_4), .in_2(bcd_adder_15_out_3), .out_3(bcd_adder_14_out_3));  // open: out_4
  BCD_adder bcd_adder_15 (
    .in_1(ram_5_data[31:28]), .in_2(ram_6_data[31:28]), .out_3(bcd_adder_15_out_3));  // open: out_4
  Multiplexer #(.width(32)) multiplexer_1 (
    .in0({bcd_adder_14_out_3, bcd_adder_12_out_3, bcd_adder_10_out_3, bcd_adder_8_out_3, bcd_adder_6_out_3, bcd_adder_4_out_3, bcd_adder_2_out_3, BCD_adder_out_3}),
    .in1({debit_7_out_2, debit_6_out_2, debit_5_out_2, debit_4_out_2, debit_3_out_2, debit_2_out_2, debit_1_out_2, debit_circuit_out_2}),
    .out(multiplexer_1_out), .sel(_0___Credit));  // open: en

  // Other names for the same wires on the sheet: B0 = _4___bit_BUS[0]; B1 = _4___bit_BUS[1]; B2 = _4___bit_BUS[2];
  //   B3 = _4___bit_BUS[3]

  // Notes on the sheet:
  //   PIN
  //   CURRENT BALANCE
  //   DEBIT or CREDIT
  //   BALANCE
  //   1 - Debit
endmodule

module Debit (
  input  [3:0] in_1,
  output [3:0] out_2
);

  wire and_1_out, and_2_out, and_3_out, and_4_out, and_5_out, and_6_out, not_1_out, not_2_out, not_3_out,
       or_1_out;

  not not_1 (not_1_out, in_1[3]);
  not not_2 (not_2_out, in_1[2]);
  not not_3 (not_3_out, in_1[1]);
  and and_1 (and_1_out, in_1[3], in_1[2], in_1[1]);
  and and_2 (and_2_out, in_1[3], not_2_out, not_3_out);
  and and_3 (and_3_out, in_1[2], or_1_out);
  or or_1 (or_1_out, not_1_out, not_3_out);
  and and_4 (and_4_out, not_2_out, in_1[1], in_1[3]);
  and and_5 (and_5_out, not_1_out, in_1[1]);
  and and_6 (and_6_out, in_1[3], in_1[2], not_3_out);
  or or_2 (out_2[3], and_1_out, and_2_out);
  or or_3 (out_2[2], and_3_out, and_4_out);
  or or_4 (out_2[1], and_5_out, and_6_out);

  assign out_2[0] = in_1[0];
endmodule

module BCD_adder (
  input  [3:0] in_1,
  input  [3:0] in_2,
  output [3:0] out_3,
  output [3:0] out_4
);

  wire adder_1_cout, and_1_out, and_2_out;
  wire [2:2] or_1_out;
  wire [3:0] adder_1_out;

  Adder #(.width(4)) adder_1 (.a(in_1), .b(in_2), .out(adder_1_out), .cout(adder_1_cout));  // open: cin
  and and_1 (and_1_out, adder_1_out[1], adder_1_out[3]);
  and and_2 (and_2_out, adder_1_out[2], adder_1_out[3]);
  or or_1 (or_1_out[2], and_1_out, and_2_out, adder_1_cout);
  Adder #(.width(4)) adder_2 (.a(adder_1_out), .b({1'b0, {2{or_1_out[2]}}, 1'b0}), .out(out_3));  // open: cin, cout
  assign out_4 = {{3{1'b0}}, or_1_out[2]};  // Bit_Extender bit_extender_1
endmodule
